# Fritzing sketch fan_PWM_NTC_controller (saved by Fritzing 0.9.3b)
breadboards: 1

parts:
  Componente2 = Arduino Nano (Rev3.0)
  R2 = Resistor [tolerance=±5% resistance=10k package=THT]
  T2 = Temperature Sensor (Thermistor) [thermistor_type=NTC package=THT]
  5V = Screw terminal - 2 pins [package=THT]
  12V = Screw terminal - 2 pins [package=THT]
  J1 = screw terminal, 4 pins
  TM1638_Led_and_Key1 = TM1638_Led_and_Key [package=THT]

nets:
  N1: Componente2.D3, J1.pin2
  N2: Componente2.D4, J1.pin1
  N3: Componente2.D8, TM1638_Led_and_Key1.DIO
  N4: Componente2.D9, TM1638_Led_and_Key1.CLK
  N5: Componente2.D10, TM1638_Led_and_Key1.STB
  GND: Componente2.GND, T2.pin_0, 5V.pin1, TM1638_Led_and_Key1.GND
  N6: Componente2.A0, R2.Pin_1, T2.pin_1
  N7: Componente2.AREF, Componente2.3V3, R2.Pin_0
  N8: 5V.pin2, TM1638_Led_and_Key1.VCC
  N9: 12V.pin1, J1.pin4
  N10: 12V.pin2, J1.pin3

notes:
  Sensor
  PWM Fan
  12v Fan
  GND Fan
